// Logisim project Calculator.circ as structural Verilog: 19 circuits, main circuit main
module main (
  output out_1,
  output out_2,
  output out_3
);

  wire _0_out, _1_out, _2_out, _3_out, _4_out, _5_out, _6_out, _7_out, _8_out, _9_out, and_1_out, and_2_out,
       and_3_out, and_4_out, and_5_out, and_6_out, and_7_out, and_8_out, and_9_out, and_10_out, and_11_out,
       and_12_out, binary_to_display_output_1_a, binary_to_display_output_1_b, binary_to_display_output_1_c,
       binary_to_display_output_1_d, binary_to_display_output_1_e, binary_to_display_output_1_f,
       binary_to_display_output_1_g, decimal_to_4_bit_converter_1_x0, decimal_to_4_bit_converter_1_x1,
       decimal_to_4_bit_converter_1_x2, decimal_to_4_bit_converter_1_x3, greaterthan_project_1_y,
       n0_or_1_second_7bit_display_1_a, n0_or_1_second_7bit_display_1_b, n0_or_1_second_7bit_display_1_c,
       n0_or_1_second_7bit_display_1_d, n0_or_1_second_7bit_display_1_e, n0_or_1_second_7bit_display_1_f,
       n0_or_1_second_7bit_display_1_g, n4_bit_adder_1_s0, n4_bit_adder_1_s1, n4_bit_adder_1_s2,
       n4_bit_adder_1_s3, n4bit_sr_latch_1_x0_2, n4bit_sr_latch_1_x1_2, n4bit_sr_latch_1_x2_2,
       n4bit_sr_latch_1_x3_2, n4bit_sr_latch_2_x0_2, n4bit_sr_latch_2_x1_2, n4bit_sr_latch_2_x2_2,
       n4bit_sr_latch_2_x3_2, not_1_out, or_1_out, or_2_out, or_3_out, or_4_out, or_5_out, RESET_out,
       select_x_or_y_1_x0, select_x_or_y_1_x1, select_x_or_y_1_x2, select_x_or_y_1_x3, select_x_or_y_1_y0,
       select_x_or_y_1_y1, select_x_or_y_1_y2, select_x_or_y_1_y3, SET_out, subtract_6_1_y0, subtract_6_1_y1,
       subtract_6_1_y2, subtract_6_1_y3;

  Button _7 (.out(_7_out));
  Button _4 (.out(_4_out));
  Button _1 (.out(_1_out));
  Button _8 (.out(_8_out));
  Button _5 (.out(_5_out));
  Button _2 (.out(_2_out));
  Button _0 (.out(_0_out));
  Button _9 (.out(_9_out));
  Button _6 (.out(_6_out));
  Button _3 (.out(_3_out));
  Decimal_to_4_Bit_Converter decimal_to_4_bit_converter_1 (
    .Zero(_0_out), .One(_1_out), .Two(_2_out), .Three(_3_out), .Four(_4_out), .Five(_5_out), .Six(_6_out),
    .Seven(_7_out), .Eight(_8_out), .Nine(_9_out), .X3(decimal_to_4_bit_converter_1_x3),
    .X2(decimal_to_4_bit_converter_1_x2), .X1(decimal_to_4_bit_converter_1_x1),
    .X0(decimal_to_4_bit_converter_1_x0));
  Button RESET (.out(RESET_out));
  Button SET (.out(SET_out));
  SR_LATCH_PROJECT sr_latch_project_1 (.in_1(SET_out), .in_2(RESET_out), .out_3(out_1), .out_4(out_2));
  Select_X_or_Y select_x_or_y_1 (
    .X_or_Y(out_2), .I3(decimal_to_4_bit_converter_1_x3), .I2(decimal_to_4_bit_converter_1_x2),
    .I1(decimal_to_4_bit_converter_1_x1), .I0(decimal_to_4_bit_converter_1_x0), .X3(select_x_or_y_1_x3),
    .X2(select_x_or_y_1_x2), .X1(select_x_or_y_1_x1), .X0(select_x_or_y_1_x0), .Y3(select_x_or_y_1_y3),
    .Y2(select_x_or_y_1_y2), .Y1(select_x_or_y_1_y1), .Y0(select_x_or_y_1_y0));
  _4bit_SR_LATCH u_4bit_sr_latch_1 (
    .X0(select_x_or_y_1_x3), .X1(select_x_or_y_1_x2), .X2(select_x_or_y_1_x1), .X3(select_x_or_y_1_x0),
    .RESET(RESET_out), .X3_2(n4bit_sr_latch_1_x3_2), .X2_2(n4bit_sr_latch_1_x2_2),
    .X1_2(n4bit_sr_latch_1_x1_2), .X0_2(n4bit_sr_latch_1_x0_2));
  _4bit_SR_LATCH u_4bit_sr_latch_2 (
    .X0(select_x_or_y_1_y3), .X1(select_x_or_y_1_y2), .X2(select_x_or_y_1_y1), .X3(select_x_or_y_1_y0),
    .RESET(RESET_out), .X3_2(n4bit_sr_latch_2_x3_2), .X2_2(n4bit_sr_latch_2_x2_2),
    .X1_2(n4bit_sr_latch_2_x1_2), .X0_2(n4bit_sr_latch_2_x0_2));
  _4_BIT_ADDER u_4_bit_adder_1 (
    .X3(n4bit_sr_latch_1_x3_2), .X2(n4bit_sr_latch_1_x2_2), .X1(n4bit_sr_latch_1_x1_2),
    .X0(n4bit_sr_latch_1_x0_2), .Y3(n4bit_sr_latch_2_x3_2), .Y2(n4bit_sr_latch_2_x2_2),
    .Y1(n4bit_sr_latch_2_x1_2), .Y0(n4bit_sr_latch_2_x0_2), .S3(n4_bit_adder_1_s3), .S2(n4_bit_adder_1_s2),
    .S1(n4_bit_adder_1_s1), .S0(n4_bit_adder_1_s0));  // open: C0
  GreaterThan_project greaterthan_project_1 (
    .X0(n4_bit_adder_1_s3), .X1(n4_bit_adder_1_s2), .X2(n4_bit_adder_1_s1), .X3(n4_bit_adder_1_s0),
    .Y(greaterthan_project_1_y));
  and and_1 (and_1_out, n4_bit_adder_1_s3, greaterthan_project_1_y);
  and and_2 (and_2_out, n4_bit_adder_1_s2, greaterthan_project_1_y);
  and and_3 (and_3_out, n4_bit_adder_1_s1, greaterthan_project_1_y);
  and and_4 (and_4_out, n4_bit_adder_1_s0, greaterthan_project_1_y);
  not not_1 (not_1_out, greaterthan_project_1_y);
  GreaterThan_project greaterthan_project_2 (
    .X0(n4_bit_adder_1_s3), .X1(n4_bit_adder_1_s2), .X2(n4_bit_adder_1_s1), .X3(n4_bit_adder_1_s0), .Y(out_3));
  Subtract_6 subtract_6_1 (
    .X0(and_1_out), .X1(and_2_out), .X2(and_3_out), .X3(and_4_out), .Y0(subtract_6_1_y0),
    .Y1(subtract_6_1_y1), .Y2(subtract_6_1_y2), .Y3(subtract_6_1_y3));
  and and_5 (and_5_out, not_1_out, n4_bit_adder_1_s3);
  and and_6 (and_6_out, not_1_out, n4_bit_adder_1_s2);
  and and_7 (and_7_out, not_1_out, n4_bit_adder_1_s1);
  and and_8 (and_8_out, not_1_out, n4_bit_adder_1_s0);
  and and_9 (and_9_out, out_3, n4_bit_adder_1_s0);
  and and_10 (and_10_out, out_3, n4_bit_adder_1_s1);
  and and_11 (and_11_out, out_3, n4_bit_adder_1_s2);
  and and_12 (and_12_out, out_3, n4_bit_adder_1_s3);
  or or_1 (or_1_out, subtract_6_1_y0, and_5_out);
  or or_2 (or_2_out, subtract_6_1_y1, and_6_out);
  or or_3 (or_3_out, subtract_6_1_y2, and_7_out);
  or or_4 (or_4_out, subtract_6_1_y3, and_8_out);
  _0_or_1_second_7bit_display u_0_or_1_second_7bit_display_1 (
    .x(or_5_out), .a(n0_or_1_second_7bit_display_1_a), .b(n0_or_1_second_7bit_display_1_b),
    .c(n0_or_1_second_7bit_display_1_c), .d(n0_or_1_second_7bit_display_1_d),
    .e(n0_or_1_second_7bit_display_1_e), .f(n0_or_1_second_7bit_display_1_f),
    .g(n0_or_1_second_7bit_display_1_g));
  or or_5 (or_5_out, and_9_out, and_10_out, and_11_out, and_12_out);
  Binary_to_display_output binary_to_display_output_1 (
    .X0(or_1_out), .X1(or_2_out), .X2(or_3_out), .X3(or_4_out), .a(binary_to_display_output_1_a),
    .b(binary_to_display_output_1_b), .c(binary_to_display_output_1_c), .d(binary_to_display_output_1_d),
    .e(binary_to_display_output_1_e), .f(binary_to_display_output_1_f), .g(binary_to_display_output_1_g));
  _7_Segment_Display u_7_segment_display_1 (
    .g(n0_or_1_second_7bit_display_1_g), .f(n0_or_1_second_7bit_display_1_f),
    .a(n0_or_1_second_7bit_display_1_a), .b(n0_or_1_second_7bit_display_1_b),
    .e(n0_or_1_second_7bit_display_1_e), .d(n0_or_1_second_7bit_display_1_d),
    .c(n0_or_1_second_7bit_display_1_c));  // open: dp
  _7_Segment_Display u_7_segment_display_2 (
    .g(binary_to_display_output_1_g), .f(binary_to_display_output_1_f), .a(binary_to_display_output_1_a),
    .b(binary_to_display_output_1_b), .e(binary_to_display_output_1_e), .d(binary_to_display_output_1_d),
    .c(binary_to_display_output_1_c));  // open: dp
endmodule

module Half_Adder_Project (
  input  X,
  input  Y,
  output Sum,
  output Carryout
);

  wire and_1_out, not_1_out, or_1_out;

  and and_1 (and_1_out, X, Y);
  or or_1 (or_1_out, X, Y);
  not not_1 (not_1_out, and_1_out);
  and and_2 (Sum, not_1_out, or_1_out);
  and and_3 (Carryout, X, Y);
endmodule

module Full_Adde_Project (
  input  X,
  input  Y,
  input  Carry_In,
  output Carry_out,
  output Sum
);

  wire half_adder_project_1_carryout, half_adder_project_1_sum, half_adder_project_2_carryout;

  Half_Adder_Project half_adder_project_1 (
    .X(X), .Y(Y), .Sum(half_adder_project_1_sum), .Carryout(half_adder_project_1_carryout));
  Half_Adder_Project half_adder_project_2 (
    .X(half_adder_project_1_sum), .Y(Carry_In), .Sum(Sum), .Carryout(half_adder_project_2_carryout));
  or or_1 (Carry_out, half_adder_project_1_carryout, half_adder_project_2_carryout);
endmodule

module binary_to_decimal_display_project (
);

  _4_BIT_ADDER u_4_bit_adder_1 ();  // open: X3, X2, X1, X0, Y3, Y2, Y1, Y0, C0, S3, S2, S1, S0
endmodule

module _4_BIT_ADDER (
  input  X3,
  input  X2,
  input  X1,
  input  X0,
  input  Y3,
  input  Y2,
  input  Y1,
  input  Y0,
  output C0,
  output S3,
  output S2,
  output S1,
  output S0
);

  wire full_adde_project_2_carry_out, full_adde_project_3_carry_out, half_adder_project_1_carryout;

  Full_Adde_Project full_adde_project_1 (
    .X(X3), .Y(Y3), .Carry_In(full_adde_project_2_carry_out), .Carry_out(C0), .Sum(S3));
  Full_Adde_Project full_adde_project_2 (
    .X(Y2), .Y(X2), .Carry_In(full_adde_project_3_carry_out), .Carry_out(full_adde_project_2_carry_out),
    .Sum(S2));
  Full_Adde_Project full_adde_project_3 (
    .X(Y1), .Y(X1), .Carry_In(half_adder_project_1_carryout), .Carry_out(full_adde_project_3_carry_out),
    .Sum(S1));
  Half_Adder_Project half_adder_project_1 (.X(Y0), .Y(X0), .Sum(S0), .Carryout(half_adder_project_1_carryout));
endmodule

module Binary_to_display_output (
  input  X0,
  input  X1,
  input  X2,
  input  X3,
  output a,
  output b,
  output c,
  output d,
  output e,
  output f,
  output g
);

  wire and_1_out, and_2_out, and_3_out, and_4_out, and_5_out, and_6_out, and_7_out, and_8_out, and_9_out,
       and_10_out, and_11_out, and_12_out, and_13_out, and_14_out, and_15_out, and_16_out, not_1_out,
       not_2_out, not_3_out, not_4_out, not_5_out, not_6_out, not_7_out, not_8_out, not_9_out, not_10_out,
       not_11_out, not_12_out, not_13_out, not_14_out, not_15_out, not_16_out, not_17_out, not_18_out,
       not_19_out, not_20_out, not_21_out;

  not not_1 (not_1_out, X1);
  and and_1 (and_1_out, not_1_out, not_2_out);
  not not_2 (not_2_out, X3);
  and and_2 (and_2_out, X1, X3);
  not not_3 (not_3_out, X1);
  not not_4 (not_4_out, X2);
  and and_3 (and_3_out, not_4_out, not_5_out);
  not not_5 (not_5_out, X3);
  and and_4 (and_4_out, X2, X3);
  not not_6 (not_6_out, X2);
  or or_1 (c, not_6_out, X3, X1);
  not not_7 (not_7_out, X1);
  and and_5 (and_5_out, not_7_out, not_8_out);
  not not_8 (not_8_out, X3);
  not not_9 (not_9_out, X1);
  and and_6 (and_6_out, not_9_out, X2);
  and and_7 (and_7_out, X2, not_10_out);
  not not_10 (not_10_out, X3);
  not not_11 (not_11_out, X2);
  and and_8 (and_8_out, X1, not_11_out, X3);
  not not_12 (not_12_out, X1);
  and and_9 (and_9_out, not_12_out, not_13_out);
  not not_13 (not_13_out, X3);
  and and_10 (and_10_out, X2, not_14_out);
  not not_14 (not_14_out, X3);
  not not_15 (not_15_out, X2);
  and and_11 (and_11_out, not_15_out, not_16_out);
  not not_16 (not_16_out, X3);
  and and_12 (and_12_out, X1, not_17_out);
  not not_17 (not_17_out, X2);
  and and_13 (and_13_out, X1, not_18_out);
  not not_18 (not_18_out, X3);
  not not_19 (not_19_out, X1);
  and and_14 (and_14_out, not_19_out, X2);
  and and_15 (and_15_out, X1, not_20_out);
  not not_20 (not_20_out, X2);
  and and_16 (and_16_out, X1, not_21_out);
  not not_21 (not_21_out, X3);
  or or_2 (a, and_1_out, X2, and_2_out, X0);
  or or_3 (b, not_3_out, and_3_out, and_4_out);
  or or_4 (d, and_5_out, and_6_out, and_7_out, and_8_out, X0);
  or or_5 (e, and_9_out, and_10_out);
  or or_6 (f, and_11_out, and_12_out, and_13_out, X0);
  or or_7 (g, and_14_out, and_15_out, and_16_out, X0);
endmodule

module GreaterThan_project (
  input  X0,
  input  X1,
  input  X2,
  input  X3,
  output Y
);

  wire and_1_out, and_2_out;

  and and_1 (and_1_out, X0, X2);
  and and_2 (and_2_out, X0, X1);
  or or_1 (Y, and_1_out, and_2_out);
endmodule

module Second_7bit_display_project (
  input  X0,
  input  X1,
  input  X2,
  input  X3,
  output S0,
  output S1,
  output S2,
  output S3
);

  wire and_1_out, and_2_out;

  and and_1 (and_1_out, X0, X2);
  and and_2 (and_2_out, X0, X1);
  or or_1 (S3, and_1_out, and_2_out);

  assign S0 = 1'b0;
  assign S1 = 1'b0;
  assign S2 = 1'b0;
endmodule

module First_7bit_display_if_greater_than_10_project (
  input  X0,
  input  X1,
  input  X2,
  input  X3,
  output S0,
  output S1,
  output S2,
  output S3
);

  wire and_2_out, and_3_out, not_1_out;

  and and_1 (S1, X0, X1, X2);
  not not_1 (not_1_out, X2);
  and and_2 (and_2_out, X0, X2, X3);
  and and_3 (and_3_out, X0, X1, X3);
  and and_4 (S2, X0, X1, not_1_out);
  or or_1 (S3, and_2_out, and_3_out);

  assign S0 = 1'b0;
endmodule

module _0_or_1_second_7bit_display (
  input  x,
  output a,
  output b,
  output c,
  output d,
  output e,
  output f,
  output g
);

  not not_1 (a, x);
  not not_2 (d, x);
  not not_3 (e, x);
  not not_4 (f, x);

  assign b = 1'b1;
  assign c = 1'b1;
  assign g = 1'b0;
endmodule

module Subtract_6 (
  input  X0,
  input  X1,
  input  X2,
  input  X3,
  output Y0,
  output Y1,
  output Y2,
  output Y3
);

  wire and_3_out, and_4_out, not_1_out;

  and and_1 (Y1, X0, X1, X2);
  and and_2 (Y2, X0, X1, not_1_out);
  not not_1 (not_1_out, X2);
  and and_3 (and_3_out, X0, X2, X3);
  and and_4 (and_4_out, X0, X1, X3);
  or or_1 (Y3, and_3_out, and_4_out);

  assign Y0 = 1'b0;
endmodule

module digit_to_bit_project (
  output out_1,
  output out_2,
  output out_3,
  output out_4
);

  wire button_1_out, button_2_out, button_3_out, button_4_out, button_5_out, button_6_out, button_7_out,
       button_8_out, button_9_out, button_10_out, button_12_out, decimal_to_4_bit_converter_1_x0,
       decimal_to_4_bit_converter_1_x1, decimal_to_4_bit_converter_1_x2, decimal_to_4_bit_converter_1_x3;

  Button button_1 (.out(button_1_out));
  Button button_2 (.out(button_2_out));
  Button button_3 (.out(button_3_out));
  Button button_4 (.out(button_4_out));
  Button button_5 (.out(button_5_out));
  Button button_6 (.out(button_6_out));
  Button button_7 (.out(button_7_out));
  Button button_8 (.out(button_8_out));
  Button button_9 (.out(button_9_out));
  Button button_10 (.out(button_10_out));
  Decimal_to_4_Bit_Converter decimal_to_4_bit_converter_1 (
    .Zero(button_7_out), .One(button_3_out), .Two(button_6_out), .Three(button_10_out), .Four(button_2_out),
    .Five(button_5_out), .Six(button_9_out), .Seven(button_1_out), .Eight(button_4_out), .Nine(button_8_out),
    .X3(decimal_to_4_bit_converter_1_x3), .X2(decimal_to_4_bit_converter_1_x2),
    .X1(decimal_to_4_bit_converter_1_x1), .X0(decimal_to_4_bit_converter_1_x0));
  Button button_11 ();  // open: out
  Button button_12 (.out(button_12_out));
  SR_LATCH_PROJECT sr_latch_project_1 (
    .in_1(decimal_to_4_bit_converter_1_x3), .in_2(button_12_out), .out_3(out_1));  // open: out_4
  SR_LATCH_PROJECT sr_latch_project_2 (
    .in_1(decimal_to_4_bit_converter_1_x2), .in_2(button_12_out), .out_3(out_2));  // open: out_4
  SR_LATCH_PROJECT sr_latch_project_3 (
    .in_1(decimal_to_4_bit_converter_1_x1), .in_2(button_12_out), .out_3(out_3));  // open: out_4
  SR_LATCH_PROJECT sr_latch_project_4 (
    .in_1(decimal_to_4_bit_converter_1_x0), .in_2(button_12_out), .out_3(out_4));  // open: out_4
endmodule

module Decimal_to_4_Bit_Converter (
  input  Zero,
  input  One,
  input  Two,
  input  Three,
  input  Four,
  input  Five,
  input  Six,
  input  Seven,
  input  Eight,
  input  Nine,
  output X3,
  output X2,
  output X1,
  output X0
);

  wire and_1_out, and_2_out, and_3_out, and_4_out, and_5_out, and_6_out, and_7_out, and_8_out, and_9_out,
       and_10_out, and_11_out, and_12_out, and_13_out, and_14_out, and_15_out, and_16_out, and_17_out,
       and_18_out, and_19_out, and_20_out, and_21_out, and_22_out, and_23_out, and_24_out, and_25_out,
       and_26_out, and_27_out, and_28_out, and_29_out, and_30_out, and_31_out, not_1_out, not_2_out,
       not_3_out, not_4_out, not_5_out, not_6_out, not_7_out, not_8_out, not_9_out, not_10_out, not_11_out,
       not_12_out, not_13_out, not_14_out, not_15_out, not_16_out, not_17_out, not_18_out, not_19_out,
       not_20_out, not_21_out, not_22_out, not_23_out, not_24_out, not_25_out, not_26_out, not_27_out,
       not_28_out, not_29_out, not_30_out, not_31_out, not_32_out, not_33_out, not_34_out, not_35_out,
       not_36_out, not_37_out, not_38_out, not_39_out, not_40_out, not_41_out, not_42_out, not_43_out,
       not_44_out, not_45_out, not_46_out, not_47_out, not_48_out, not_49_out;

  and and_1 (and_1_out, Six, Seven);
  and and_2 (and_2_out, Five, Seven);
  and and_3 (and_3_out, Four, Seven);
  and and_4 (and_4_out, Three, Seven);
  and and_5 (and_5_out, Two, Seven);
  and and_6 (and_6_out, One, Seven);
  and and_7 (and_7_out, Zero, Seven);
  not not_1 (not_1_out, Zero);
  not not_2 (not_2_out, One);
  not not_3 (not_3_out, Two);
  not not_4 (not_4_out, Three);
  not not_5 (not_5_out, Eight);
  not not_6 (not_6_out, Nine);
  not not_7 (not_7_out, Zero);
  not not_8 (not_8_out, One);
  not not_9 (not_9_out, Four);
  not not_10 (not_10_out, Eight);
  not not_11 (not_11_out, Nine);
  not not_12 (not_12_out, Zero);
  not not_13 (not_13_out, One);
  not not_14 (not_14_out, Four);
  not not_15 (not_15_out, Eight);
  not not_16 (not_16_out, Nine);
  not not_17 (not_17_out, Zero);
  not not_18 (not_18_out, Two);
  not not_19 (not_19_out, Four);
  not not_20 (not_20_out, Five);
  not not_21 (not_21_out, Six);
  not not_22 (not_22_out, Eight);
  not not_23 (not_23_out, Zero);
  not not_24 (not_24_out, Two);
  not not_25 (not_25_out, Four);
  not not_26 (not_26_out, Five);
  not not_27 (not_27_out, Six);
  not not_28 (not_28_out, Eight);
  not not_29 (not_29_out, Zero);
  not not_30 (not_30_out, One);
  not not_31 (not_31_out, Two);
  not not_32 (not_32_out, Three);
  not not_33 (not_33_out, Four);
  not not_34 (not_34_out, Six);
  not not_35 (not_35_out, Seven);
  not not_36 (not_36_out, Eight);
  not not_37 (not_37_out, Nine);
  not not_38 (not_38_out, Zero);
  not not_39 (not_39_out, Two);
  not not_40 (not_40_out, Four);
  not not_41 (not_41_out, Five);
  not not_42 (not_42_out, Six);
  not not_43 (not_43_out, Eight);
  not not_44 (not_44_out, Zero);
  not not_45 (not_45_out, Two);
  not not_46 (not_46_out, Four);
  not not_47 (not_47_out, Five);
  not not_48 (not_48_out, Six);
  not not_49 (not_49_out, Eight);
  or or_1 (X3, Nine, Eight, and_1_out, and_2_out, and_3_out, and_4_out, and_5_out, and_6_out, and_7_out);
  and and_8 (and_8_out, not_1_out, not_2_out, not_3_out, not_4_out, Seven, not_5_out, not_6_out);
  and and_9 (and_9_out, Three, Nine);
  and and_10 (and_10_out, Three, Eight);
  and and_11 (and_11_out, Two, Three);
  and and_12 (and_12_out, One, Three);
  and and_13 (and_13_out, Zero, Three);
  and and_14 (and_14_out, Eight, Nine);
  and and_15 (and_15_out, not_7_out, not_8_out, not_9_out, Seven, not_10_out, not_11_out);
  and and_16 (and_16_out, Five, Nine);
  and and_17 (and_17_out, Five, Eight);
  and and_18 (and_18_out, Four, Nine);
  and and_19 (and_19_out, Four, Five);
  and and_20 (and_20_out, not_12_out, not_13_out, Three, not_14_out, not_15_out, not_16_out);
  and and_21 (and_21_out, One, Eight);
  and and_22 (and_22_out, One, Five);
  and and_23 (and_23_out, One, Four);
  and and_24 (and_24_out, Zero, Nine);
  and and_25 (and_25_out, Zero, Five);
  and and_26 (and_26_out, Zero, One);
  and and_27 (and_27_out, not_17_out, not_18_out, not_19_out, not_20_out, not_21_out, not_22_out, Nine);
  and and_28 (and_28_out, not_23_out, not_24_out, not_25_out, not_26_out, not_27_out, Seven, not_28_out);
  and and_29 (and_29_out, not_29_out, not_30_out, not_31_out, not_32_out, not_33_out, Five, not_34_out, not_35_out, not_36_out, not_37_out);
  and and_30 (and_30_out, not_38_out, not_39_out, Three, not_40_out, not_41_out, not_42_out, not_43_out);
  and and_31 (and_31_out, not_44_out, One, not_45_out, not_46_out, not_47_out, not_48_out, not_49_out);
  or or_2 (X2, and_8_out, Six, Five, Four, and_9_out, and_10_out, and_11_out, and_12_out, and_13_out);
  or or_3 (X0, and_27_out, and_28_out, and_29_out, and_30_out, and_31_out);
  or or_4 (X1, and_14_out, and_15_out, Six, and_16_out, and_17_out, and_18_out, and_19_out, and_20_out, Two, and_21_out, and_22_out, and_23_out, and_24_out, and_25_out, and_26_out);
endmodule

module subtract (
  input  X0,
  input  X1,
  input  X2,
  input  X3,
  output Y0,
  output Y1,
  output Y2,
  output Y3
);

  wire and_1_out, and_2_out, and_3_out, and_4_out, and_5_out, and_6_out, and_7_out, and_8_out, and_9_out,
       not_1_out, not_2_out, not_3_out, not_4_out, not_5_out, not_6_out, not_7_out, not_8_out, not_9_out;

  not not_1 (not_1_out, X0);
  not not_2 (not_2_out, X1);
  not not_3 (not_3_out, X2);
  not not_4 (not_4_out, X3);
  not not_5 (not_5_out, X1);
  and and_1 (and_1_out, not_5_out, not_6_out, not_7_out);
  not not_6 (not_6_out, X2);
  not not_7 (not_7_out, X3);
  and and_2 (and_2_out, X1, X3);
  and and_3 (and_3_out, X1, X2);
  not not_8 (not_8_out, X2);
  and and_4 (and_4_out, not_8_out, not_9_out);
  not not_9 (not_9_out, X3);
  and and_5 (and_5_out, X2, X3);
  not not_10 (Y3, X3);
  and and_6 (and_6_out, not_1_out, not_2_out, not_3_out, not_4_out);
  and and_7 (and_7_out, X0, X3);
  and and_8 (and_8_out, X0, X2);
  and and_9 (and_9_out, X0, X1);
  or or_1 (Y1, and_1_out, and_2_out, and_3_out);
  or or_2 (Y2, and_4_out, and_5_out);
  or or_3 (Y0, and_6_out, and_7_out, and_8_out, and_9_out);
endmodule

module SR_LATCH_PROJECT (
  input  in_1,
  input  in_2,
  output out_3,
  output out_4
);

  wire and_1_out, and_2_out, and_3_out, and_4_out, not_1_out, not_2_out;

  and and_1 (and_1_out, in_1, 1'b1);
  and and_2 (and_2_out, 1'b1, in_2);
  not not_1 (not_1_out, and_1_out);
  not not_2 (not_2_out, and_2_out);
  not not_3 (out_3, and_3_out);
  and and_3 (and_3_out, not_1_out, out_4);
  not not_4 (out_4, and_4_out);
  and and_4 (and_4_out, out_3, not_2_out);
endmodule

module _4bit_SR_LATCH (
  input  X0,
  input  X1,
  input  X2,
  input  X3,
  input  RESET,
  output X3_2,
  output X2_2,
  output X1_2,
  output X0_2
);

  SR_LATCH_PROJECT sr_latch_project_1 (.in_1(X0), .in_2(RESET), .out_3(X3_2));  // open: out_4
  SR_LATCH_PROJECT sr_latch_project_2 (.in_1(X1), .in_2(RESET), .out_3(X2_2));  // open: out_4
  SR_LATCH_PROJECT sr_latch_project_3 (.in_1(X2), .in_2(RESET), .out_3(X1_2));  // open: out_4
  SR_LATCH_PROJECT sr_latch_project_4 (.in_1(X3), .in_2(RESET), .out_3(X0_2));  // open: out_4
endmodule

module Set (
  input  First,
  input  Second,
  input  Third,
  input  Fourth,
  output X1,
  output X0
);

  or or_1 (X1, Fourth, Third);
  or or_2 (X0, Fourth, Second);
endmodule

module _8_and_gates_and_4_or_gates_project (
  input  Q,
  input  A3,
  input  A2,
  input  A1,
  input  A0,
  input  B3,
  input  B2,
  input  B1,
  input  B0,
  output X3,
  output X2,
  output X1,
  output X0
);

  wire and_1_out, and_2_out, and_3_out, and_4_out, and_5_out, and_6_out, and_7_out, and_8_out, not_1_out,
       not_2_out, not_3_out, not_4_out;

  and and_1 (and_1_out, A3, Q);
  and and_2 (and_2_out, A2, Q);
  and and_3 (and_3_out, A1, Q);
  and and_4 (and_4_out, A0, Q);
  and and_5 (and_5_out, B3, not_1_out);
  not not_1 (not_1_out, Q);
  and and_6 (and_6_out, B2, not_2_out);
  not not_2 (not_2_out, Q);
  and and_7 (and_7_out, B1, not_3_out);
  not not_3 (not_3_out, Q);
  and and_8 (and_8_out, B0, not_4_out);
  not not_4 (not_4_out, Q);
  or or_1 (X3, and_1_out, and_8_out);
  or or_2 (X2, and_2_out, and_7_out);
  or or_3 (X1, and_3_out, and_6_out);
  or or_4 (X0, and_4_out, and_5_out);
endmodule

module Select_X_or_Y (
  input  X_or_Y,
  input  I3,
  input  I2,
  input  I1,
  input  I0,
  output X3,
  output X2,
  output X1,
  output X0,
  output Y3,
  output Y2,
  output Y1,
  output Y0
);

  wire not_1_out, not_2_out, not_3_out, not_4_out;

  not not_1 (not_1_out, X_or_Y);
  not not_2 (not_2_out, X_or_Y);
  not not_3 (not_3_out, X_or_Y);
  not not_4 (not_4_out, X_or_Y);
  and and_1 (X3, I3, X_or_Y);
  and and_2 (X2, I2, X_or_Y);
  and and_3 (X1, I1, X_or_Y);
  and and_4 (X0, I0, X_or_Y);
  and and_5 (Y3, I3, not_1_out);
  and and_6 (Y2, I2, not_2_out);
  and and_7 (Y1, I1, not_3_out);
  and and_8 (Y0, I0, not_4_out);
endmodule
